# Fritzing sketch ESP Fan (saved by Fritzing 0.9.10b)
circuit board: 8.46667cm x 5.64444cm
breadboards: 1

parts:
  JACK1 = 2.1mm Barrel Jack with Terminal Block
  Mod1 = Amica NodeMCU DEVKIT 1.0
  M1 = RioRand LM2596
  DHT1 = DHT11 Humitidy and Temperature Sensor
  F1 = Fan - 4 wire [package=THT]
  F3 = Fan - 4 wire [package=THT]
  F2 = Fan - 4 wire [package=THT]

nets:
  N1: JACK1.POS, M1.Pin_1, F1.Power, F3.Power, F2.Power
  GND: JACK1.NEG, Mod1.pin2, Mod1.pin_9, Mod1.pin_25, Mod1.pin_29, M1.Pin_2, M1.Pin_4, DHT1.GND, F1.GND, F3.GND, F2.GND
  N2: Mod1.pin1, Mod1.pin_10, Mod1.pin_26
  N3: Mod1.pin5, F1.PWM, F3.PWM, F2.PWM
  N4: Mod1.pin_14, DHT1.DATA
  N5: Mod1.pin_30, M1.Pin_3, DHT1.VDD

custom parts:
  DHT11 Humitidy and Temperature Sensor: DHT11 Humidity and Temperature Sensor
  Fan - 4 wire: Fan, 4 wire with tach.
